# Fritzing sketch full (saved by Fritzing 0.9.3b)
breadboards: 1

parts:
  U1 = ESP8266 NodeMCU LoLin module
  Part1 = Arduino Nano (Rev3.0) (ICSP)
  GY1 = MPU-6050 Board GY-521 [form="♀ (female)" package=THT]
  R1 = Basic Flex Resistor
  R2 = Resistor [tolerance=±5% resistance=10 package="0603 [SMD]"]
  R3 = Basic Flex Resistor
  R4 = Basic Flex Resistor
  R5 = Basic Flex Resistor
  R6 = Basic Flex Resistor
  R7 = Resistor [tolerance=±5% resistance=10 package="0603 [SMD]"]
  R8 = Resistor [tolerance=±5% resistance=10 package="0603 [SMD]"]
  R9 = Resistor [tolerance=±5% resistance=10 package="0603 [SMD]"]
  R10 = Resistor [tolerance=±5% resistance=10 package="0603 [SMD]"]
  U2 = SWITCH-SPST-2 [package=switch-spst-vertical]
  U3 = SWITCH-SPST-2 [package=switch-spst-vertical]
  R11 = Resistor [tolerance=±5% resistance=100 package="0603 [SMD]"]
  R12 = Resistor [tolerance=±5% resistance=100 package="0603 [SMD]"]
  U4 = SWITCH-SPST-2 [package=switch-spst-vertical]
  R13 = Resistor [tolerance=±5% resistance=100 package="0603 [SMD]"]

nets:
  N1: U1.D5, Part1.D13/SCK
  N2: U1.D6, Part1.D12/MISO
  N3: U1.D7, Part1.D11/MOSI
  N4: U1.D8, Part1.D10
  GND: U1.GND, Part1.GND, GY1.pin2, R2.Pin_0, R7.Pin_0, R8.Pin_0, R9.Pin_0, R10.Pin_0, R11.Pin_0, R12.Pin_0, R13.Pin_0
  N5: Part1.D2, U4.O
  N6: Part1.D3, U3.O
  N7: Part1.D4, U2.O
  N8: Part1.5V, GY1.pin1, R1.Pin_2, R3.Pin_2, R4.Pin_2, R5.Pin_2, R6.Pin_2, U2.P, U3.P, R11.Pin_1, R12.Pin_1, U4.P, R13.Pin_1
  N9: Part1.A7, R6.pin_1, R10.Pin_1
  N10: Part1.A6, R5.pin_1, R9.Pin_1
  N11: Part1.A5, GY1.pin3
  N12: Part1.A4, GY1.pin4
  N13: Part1.A3, R4.pin_1, R8.Pin_1
  N14: Part1.A2, R3.pin_1, R7.Pin_1
  N15: Part1.A1, R1.pin_1, R2.Pin_1

notes:
  Contact Sensors
  Flex Sensors
  Gyroscope

custom parts:
  ESP8266 NodeMCU LoLin module: ESP8266 based NodeMCU
  MPU-6050 Board GY-521: Acelerometro y Giroscopio MPU-6050 Board GY-521
